# Fritzing sketch SENSOR DE COR (saved by Fritzing 0.9.2b)

parts:
  e-radionica1 = TCS230 Color Sensor [part_number=101209]
  Componente1 = Arduino Uno (Rev3)
  J1 = Basic Servo

nets:
  GND: e-radionica1.Gnd, e-radionica1.OE, Componente1.GND, J1.gnd
  N1: e-radionica1.S1, Componente1.D9_PWM
  N2: e-radionica1.S0, Componente1.D8
  N3: e-radionica1.S3, Componente1.D11_PWM/MOSI
  N4: e-radionica1.S2, Componente1.D12/MISO
  N5: e-radionica1.Out, Componente1.D10_PWM/SS
  VCC: e-radionica1.Vcc, Componente1.5V, J1.vcc
  N6: Componente1.D7, J1.pulse

custom parts:
  TCS230 Color Sensor: TCS230
